# Fritzing sketch photobooth_sketch (saved by Fritzing 0.9.3b)
breadboards: 1

parts:
  Raspberry_Pi1 = Raspberry Pi B+
  LED1 = LED - 5mm [color="Red (633nm)" package="5 mm [THT]"]
  R1 = Resistor [tolerance=±5% resistance=220 package=THT]
  S1 = Pushbutton [package="[THT]"]
  LED2 = LED - 5mm [color="Yellow (595nm)" package="5 mm [THT]"]

nets:
  N1: Raspberry_Pi1.GPIO17, LED2.anode
  N2: Raspberry_Pi1.GPIO23, LED1.anode
  N3: Raspberry_Pi1.GPIO18, Raspberry_Pi1.5V, S1.Pin_1, S1.Pin_2
  N4: Raspberry_Pi1.GND, R1.Pin_0
  N5: LED1.cathode, R1.Pin_1, LED2.cathode
